# Fritzing sketch Covoiturage-V1 (saved by Fritzing 0.9.9b)
breadboards: 1

parts:
  Composant1 = RFID-RC522-v3  # not connected
  M1 = NEO-6M GPS Module [part_number=GY-GPS6MV2]  # not connected
  Squix1 = OLED 0.96" 128x64 I2C SSD1306  # not connected
  LED1 = LED - 5mm [color="Red (633nm)" current=0.030 package="5 mm [THT]"]  # not connected
  LED2 = LED - 5mm [color="Red (633nm)" current=0.030 package="5 mm [THT]"]  # not connected
  S2 = Pushbutton [package="[THT]"]
  Espessif_Serial_Wifi_Modul_1 = ESP8266 ESP01 [part_number=ESP8266 package=THT]  # not connected
  S3 = Pushbutton [package="[THT]"]
  DFPlayer_Mini1 = DFPlayer MINI [package="DIP (Dual Inline) [THT]"]  # not connected
  Mod1 = Raspberry Pi Pico  # not connected

nets:
  N1: S2.Pin_1, S2.Pin_2
  N2: S2.Pin_3, S2.Pin_4
  N3: S3.Pin_1, S3.Pin_2
  N4: S3.Pin_3, S3.Pin_4

custom parts:
  RFID-RC522-v3: A simple China made RFID-RC522 Reader (6x4 cm); do check the pin labels, as this is a MFRC522 based clone.
  NEO-6M GPS Module: GY-GPS6MV2 NEO-6M GPS Module Module based on U-blox NEO-6M GPS engine, incorporating regulator for 3.3-5V DC input, MS621FE-compatible rechargeable battery for backup and EEPROM for storing configuration settings. Links: NEO-6 series product information page NEO-6 Datasheet
  ESP8266 ESP01: Generic WiFi Module based on the ESP8266 with onboard PCB antenna and UART communications
  DFPlayer MINI: MP3 module by DFRobot.com for playing Music from an SD-Card. Supports WAV and MP3 files.
  Raspberry Pi Pico: Raspberry Pi Pico. Based around the RP2040 microcontroller the Pico is a low cost microcontroller device bringing Raspberry Pi quality, cost, and easy of use to the microcontroller space. Jan 2021, Split part in to two versions: tht (this one) and SMD. This one will drill holes for a .1 in header in pcb to allow plugging in the module as well as providing pads to solder the module to the top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
