# Fritzing sketch Covoiturage-V2 (saved by Fritzing 0.9.9b)
breadboards: 1

parts:
  M1 = NEO-6M GPS Module [part_number=GY-GPS6MV2]
  Squix1 = OLED 0.96" 128x64 I2C SSD1306
  LED1 = LED - 5mm [color="Red (633nm)" current=0.030 package="5 mm [THT]"]
  LED2 = LED - 5mm [color="Red (633nm)" current=0.030 package="5 mm [THT]"]
  S2 = Pushbutton [package="[THT]"]
  S3 = Pushbutton [package="[THT]"]
  R1 = Resistor [tolerance=±5% power=0.25 resistance=220 package=THT]
  R2 = Resistor [tolerance=±5% power=0.25 resistance=220 package=THT]
  Mod1 = Raspberry Pi Pico
  Composant2 = Bluetooth HC-06 Macho
  Composant1 = RFID-RC522-v3

nets:
  GND: M1.GND, Squix1.GND, LED1.anode, LED2.anode, S2.Pin_1, S2.Pin_2, S3.Pin_1, S3.Pin_2, Mod1.pin_3, Mod1.pin_8, Mod1.pin_13, Mod1.pin_18, Mod1.pin_20, Mod1.pin_23, Mod1.pin_28, Mod1.pin_33, Mod1.pin_38, Mod1.pin_42, Composant2.GND, Composant1.GND
  N1: M1.Tx, Mod1.pin_1
  N2: M1.Rx, Mod1.pin_2
  VCC: M1.Vcc, Squix1.VCC, Composant2.VCC, Composant1.3.3V
  N3: Squix1.SCL, Mod1.pin_32
  N4: Squix1.SCA, Mod1.pin_31
  N5: LED1.cathode, R1.Pin_1
  N6: LED2.cathode, R2.Pin_1
  N7: S2.Pin_3, S2.Pin_4
  N8: S3.Pin_3, S3.Pin_4, Mod1.pin_19
  N9: R1.Pin_0, Mod1.pin_22
  N10: R2.Pin_0, Mod1.pin_21
  N11: Mod1.pin_5, Composant1.MOSI
  N12: Mod1.pin_6, Composant1.MISO
  N13: Mod1.pin_11, Composant2.TXD
  N14: Mod1.pin_12, Composant2.RXD
  N15: Mod1.pin_16, Composant1.SDA
  N16: Mod1.pin_17, Composant1.SCK
  N17: Mod1.pin_29, Composant1.RST

notes:
  RFID
  Uart0
  GPS
  RX inutile
  Uart? SPI?
  Bouton1
  Bouton2
  Led vert + rouge

custom parts:
  NEO-6M GPS Module: GY-GPS6MV2 NEO-6M GPS Module Module based on U-blox NEO-6M GPS engine, incorporating regulator for 3.3-5V DC input, MS621FE-compatible rechargeable battery for backup and EEPROM for storing configuration settings. Links: NEO-6 series product information page NEO-6 Datasheet
  Raspberry Pi Pico: Raspberry Pi Pico. Based around the RP2040 microcontroller the Pico is a low cost microcontroller device bringing Raspberry Pi quality, cost, and easy of use to the microcontroller space. Jan 2021, Split part in to two versions: tht (this one) and SMD. This one will drill holes for a .1 in header in pcb to allow plugging in the module as well as providing pads to solder the module to the top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
  RFID-RC522-v3: A simple China made RFID-RC522 Reader (6x4 cm); do check the pin labels, as this is a MFRC522 based clone.
